# Fritzing sketch Circuito (saved by Fritzing 1.0.2b)
perfboards: 4

parts:
  DHT1 = DHT11 Humitidy and Temperature Sensor (3 pins)  # not connected
  J1 = female pin header, 2 pins [form="♀ (female)"]
  J2 = female pin header, 2 pins [form="♀ (female)"]
  J3 = female pin header, 2 pins [form="♀ (female)"]  # not connected
  J4 = female pin header, 2 pins [form="♀ (female)"]  # not connected
  J5 = female pin header, 2 pins [form="♀ (female)"]  # not connected
  J6 = female pin header, 2 pins [form="♀ (female)"]
  J7 = female pin header, 2 pins [form="♀ (female)"]  # not connected
  J8 = female pin header, 2 pins [form="♀ (female)"]  # not connected
  J9 = female pin header, 2 pins [form="♀ (female)"]  # not connected
  J10 = female pin header, 2 pins [form="♀ (female)"]  # not connected
  J11 = female pin header, 2 pins [form="♀ (female)"]  # not connected
  J12 = female pin header, 2 pins [form="♀ (female)"]  # not connected
  J13 = female pin header, 2 pins [form="♀ (female)"]  # not connected
  J14 = female pin header, 2 pins [form="♀ (female)"]  # not connected
  J15 = female pin header, 2 pins [form="♀ (female)"]  # not connected
  J16 = female pin header, 2 pins [form="♀ (female)"]  # not connected
  J17 = female pin header, 2 pins [form="♀ (female)"]  # not connected
  JP1 = Header 3 [package=molex-1x3_lock]
  JP2 = Header 3 [package=molex-1x3_lock]  # not connected
  J18 = female pin header, 2 pins [form="♀ (female)"]
  J24 = female pin header, 2 pins [form="♀ (female)"]
  J25 = Dagu DGServo 9g header connector (female) [package=THT]  # not connected
  J26 = Dagu DGServo 9g header connector (female) [package=THT]
  J27 = Dagu DGServo 9g header connector (female) [package=THT]
  J28 = Dagu DGServo 9g header connector (female) [package=THT]
  Grove1 = Grove Dust Sensor  # not connected
  J29 = Dagu DGServo 9g header connector (female) [package=THT]  # not connected
  J30 = female pin header, 2 pins [form="♀ (female)"]  # not connected
  J32 = female pin header, 2 pins [form="♀ (female)"]  # not connected
  J33 = female pin header, 2 pins [form="♀ (female)"]  # not connected
  J34 = female pin header, 2 pins [form="♀ (female)"]  # not connected
  J35 = female pin header, 2 pins [form="♀ (female)"]  # not connected
  J36 = Dagu DGServo 9g header connector (female) [package=THT]  # not connected
  J37 = female pin header, 2 pins [form="♀ (female)"]  # not connected
  J38 = female pin header, 2 pins [form="♀ (female)"]
  M3 = Keyestudio CCS811 [part_number="Keyestudio #KS0457"]  # not connected
  GY1 = MPU-6050 Board GY-521 [form="♀ (female)" package=THT]
  M4 = mics-6814

nets:
  N1: J1.pin1, J18.pin2
  N2: J1.pin2, J6.pin1
  N3: J2.pin1, GY1.pin4
  N4: J2.pin2, GY1.pin5
  N5: JP1.2, J38.pin2
  N6: J24.pin1, M4.+5V
  N7: J24.pin2, M4.GND
  N8: J26.gnd, GY1.pin6
  N9: J26.Vcc, GY1.pin7
  N10: J26.pulse, GY1.pin8
  N11: J27.gnd, GY1.pin1
  N12: J27.Vcc, GY1.pin2
  N13: J27.pulse, GY1.pin3
  N14: J28.gnd, M4.NO2
  N15: J28.Vcc, M4.NH3
  N16: J28.pulse, M4.CO

notes:
  MICS-6814
  CO
  NH3
  NO2
  Shinyei Dust sensor:
  Polveri sottili (TVOC)
  DHT11:
  Umidità
  Air quality sensor
  (Sensore mancante su Fritzing)
  GY-BMP280:
  Pressione
  Temperatura
  Pressione
  SEN-CCS811:
  CO2
  TVOC

custom parts:
  DHT11 Humitidy and Temperature Sensor (3 pins): DHT11 Humidity and Temperature Sensor (3 pins).
  Grove Dust Sensor: PPD42 Grove Dust Sensor
  Keyestudio CCS811: Breathe easy - we finally have an I2C VOC/eCO2 sensor in the Adafruit shop! Add air quality monitoring to your project and with an Keyestudio CCS811 Air Quality Sensor Breakout. This sensor from AMS is a gas sensor that can detect a wide range of Volatile Organic Compounds (VOCs) and is intended for indoor air quality monitoring. When connected to your microcontroller (running our library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
  MPU-6050 Board GY-521: Acelerometro y Giroscopio MPU-6050 Board GY-521
  mics-6814: The MICS6814 sensor comprises three semiconductor gas sensors in a single package, and can detect three different groups of gases that are referred to in the datasheet as reducing, oxidising, and NH3. The major gases/vapours that the sensor detects are: carbon monoxide (reducing), nitrogen dioxide (oxidising), and ammonia (NH3), but it is also sensitive to others, including hydrogen, ethanol,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
